# Fritzing sketch msat-wiring (saved by Fritzing 1.0.5)
breadboards: 2

parts:
  U1 = ESP32-38PinWide [part_number=ESP32-38PinWide]
  DS1 = DS18B20 1-Wire Temperature Sensor Probe  # not connected
  S1 = Pushbutton [package="[THT]"]
  M1 = RioRand LM2596  # not connected
  U2 = MAX485 [package=dil08]  # not connected
  Part1 = HX711 Weighing Sensor Module  # not connected
  Part2 = ADS1115  # not connected
  WeMos_D1_Mini_Relay_Shield_V1 = WeMos D1 Mini Relay Shield V2  # not connected
  WeMos_D1_Mini_Relay_Shield_V2 = WeMos D1 Mini Relay Shield V2  # not connected
  A1 = GY33 Color Recognition Sensor Module  # not connected

nets:
  N1: U1.GPIO5, S1.Pin_1, S1.Pin_2
  N2: S1.Pin_3, S1.Pin_4

custom parts:
  ESP32-38PinWide: Generic 38-Pin ESP32 with wide format (only access to one side of pins on a breadboard) based on Stephen Lilley's HiLetgo ESP-WROOM-32 ESP32 ESP-32S Development Board.
  ADS1115: ADC ADS1115
  GY33 Color Recognition Sensor Module: GY33 Color Recognition Sensor Module.
